# Fritzing sketch lab0-stm32f401 (saved by Fritzing 0.9.4)
breadboards: 1

parts:
  LED1 = LED - 5mm [color="Red (633nm)" package="5 mm [THT]"]
  R1 = Resistor [tolerance=±5% resistance=220 package=THT]
  J1 = STM32 Nucleo boards

nets:
  N1: LED1.cathode, R1.Pin_1
  N2: LED1.anode, J1.PC3
  N3: R1.Pin_0, J1.GND
