# Fritzing sketch lab5-stm32f401 (saved by Fritzing 0.9.4)
breadboards: 1

parts:
  J1 = STM32 Nucleo boards
  7_Segment1 = 7 Segment Display
  7_Segment2 = 7 Segment Display
  SW1 = DIP Switch 8 Position [package=dipswitch-08]
  R2 = Resistor [tolerance=±5% resistance=220 package="0603 [SMD]"]
  R3 = Resistor [tolerance=±5% resistance=220 package="0603 [SMD]"]
  R4 = Resistor [tolerance=±5% resistance=220 package="0603 [SMD]"]
  R5 = Resistor [tolerance=±5% resistance=220 package="0603 [SMD]"]
  R6 = Resistor [tolerance=±5% resistance=220 package="0603 [SMD]"]
  S1 = Square Pushbutton

nets:
  N1: J1.PC6, 7_Segment1.Segment_B
  N2: J1.PC5, 7_Segment1.Segment_A#10
  N3: J1.PB2, SW1.3, R5.Pin_1
  N4: J1.PB1, SW1.2, R3.Pin_1
  N5: J1.PC4, 7_Segment1.Segment_D
  N6: J1.PA5, 7_Segment2.Segment_A#10
  N7: J1.PA6, 7_Segment2.Segment_B
  N8: J1.PB3, SW1.4, R4.Pin_1
  N9: J1.PA2, 7_Segment2.common_cathode#3
  N10: J1.PA3, 7_Segment2.Segment_E
  N11: J1.PA0, 7_Segment2.Segment_A#1
  N12: J1.PA1, 7_Segment2.Segment_F
  N13: J1.PA4, 7_Segment2.Segment_D
  N14: J1.PB0, SW1.1, R2.Pin_1
  N15: J1.PC1, 7_Segment1.Segment_F
  N16: J1.PC0, 7_Segment1.Segment_A#1
  N17: J1.PC13, R6.Pin_1
  N18: J1.PC2, 7_Segment1.common_cathode#3
  N19: J1.PC3, 7_Segment1.Segment_E
  N20: 7_Segment1.Segment_DP, 7_Segment2.Segment_DP, R2.Pin_0, R3.Pin_0, R4.Pin_0, R5.Pin_0, R6.Pin_0
  N21: SW1.13, SW1.14, SW1.15, SW1.16, S1.leg0, S1.leg1
