# Fritzing sketch Lab7 (saved by Fritzing 0.9.4)
breadboards: 1

parts:
  J1 = STM32 Nucleo boards
  LCD1 = LCD screen
  R1 = Rotary Potentiometer (Small) [maximum_resistance=100kΩ package=THT]

nets:
  N1: J1.PC6, LCD1.DB6
  N2: J1.PC5, LCD1.DB5
  N3: J1.PC4, LCD1.DB4
  N4: J1.PB6, LCD1.R/W
  N5: J1.PC7, LCD1.DB7
  N6: J1.PB5, LCD1.RS
  N7: J1.PC1, LCD1.DB1
  N8: J1.PC0, LCD1.DB0
  N9: J1.PB7, LCD1.E
  N10: J1.PC2, LCD1.DB2
  N11: J1.PC3, LCD1.DB3
  N12: LCD1.VSS, LCD1.LED-, R1.leg1
  N13: LCD1.VDD, LCD1.LED+, R1.leg2
  N14: LCD1.V0, R1.wiper
